// Logisim project DecodeIR.circ as structural Verilog: 1 circuit, main circuit DecodeIR
module DecodeIR (
  input  [31:0] IR,
  output WriteReg,
  output Store,
  output Load,
  output CTRL,
  output [2:0] GetOp,
  output [15:0] JMPAddress
);

  Decoder #(.select(2), .enable("false")) decoder_1 (
    .out0(WriteReg), .out1(Store), .out2(Load), .out3(CTRL), .sel(IR[1:0]));
  assign JMPAddress = IR[5] ? IR[31:16] : 16'bz;  // Controlled_Buffer controlled_buffer_1

  assign GetOp = IR[4:2];
endmodule
