// Logisim project Registres.circ as structural Verilog: 1 circuit, main circuit main
module Registres (
  input  [15:0] IN,
  input  [2:0] SR1,
  input  [2:0] SR2,
  input  [2:0] DR,
  input  WriteReg,
  input  Clock,
  input  Reset,
  output [15:0] R0,
  output [15:0] OUT_SR1,
  output [15:0] R1,
  output [15:0] R2,
  output [15:0] R3,
  output [15:0] OUT_SR2,
  output [15:0] R4,
  output [15:0] R5,
  output [15:0] OUT_DR,
  output [15:0] R6,
  output [15:0] R7
);

  wire demultiplexer_1_out0, demultiplexer_1_out1, demultiplexer_1_out2, demultiplexer_1_out3,
       demultiplexer_1_out4, demultiplexer_1_out5, demultiplexer_1_out6, demultiplexer_1_out7;
  wire [15:0] n16_bit_transistor_1_p3, n16_bit_transistor_2_p3, n16_bit_transistor_3_p3,
       n16_bit_transistor_4_p3, n16_bit_transistor_5_p3, n16_bit_transistor_6_p3, n16_bit_transistor_7_p3,
       n16_bit_transistor_8_p3;

  Demultiplexer #(.select(3)) demultiplexer_1 (
    .out0(demultiplexer_1_out0), .out1(demultiplexer_1_out1), .out2(demultiplexer_1_out2),
    .out3(demultiplexer_1_out3), .out4(demultiplexer_1_out4), .out5(demultiplexer_1_out5),
    .out6(demultiplexer_1_out6), .out7(demultiplexer_1_out7), .in(Clock), .sel(DR), .en(WriteReg));
  // _16_bit_transistor 16_bit_transistor_1: pin names not known; wires that end beside it: IN, demultiplexer_1_out0, n16_bit_transistor_1_p3
  // _16_bit_transistor 16_bit_transistor_2: pin names not known; wires that end beside it: IN, demultiplexer_1_out1, n16_bit_transistor_2_p3
  // _16_bit_transistor 16_bit_transistor_3: pin names not known; wires that end beside it: IN, demultiplexer_1_out2, n16_bit_transistor_3_p3
  // _16_bit_transistor 16_bit_transistor_4: pin names not known; wires that end beside it: IN, demultiplexer_1_out3, n16_bit_transistor_4_p3
  // _16_bit_transistor 16_bit_transistor_5: pin names not known; wires that end beside it: IN, demultiplexer_1_out4, n16_bit_transistor_5_p3
  // _16_bit_transistor 16_bit_transistor_6: pin names not known; wires that end beside it: IN, demultiplexer_1_out5, n16_bit_transistor_6_p3
  // _16_bit_transistor 16_bit_transistor_7: pin names not known; wires that end beside it: IN, demultiplexer_1_out6, n16_bit_transistor_7_p3
  // _16_bit_transistor 16_bit_transistor_8: pin names not known; wires that end beside it: IN, demultiplexer_1_out7, n16_bit_transistor_8_p3
  Register #(.width(16), .trigger("falling")) u_R0 (
    .D(n16_bit_transistor_1_p3), .Q(R0), .clk(Clock), .clr(Reset));  // open: en
  Register #(.width(16), .trigger("falling")) u_R1 (
    .D(n16_bit_transistor_2_p3), .Q(R1), .clk(Clock), .clr(Reset));  // open: en
  Register #(.width(16), .trigger("falling")) u_R2 (
    .D(n16_bit_transistor_3_p3), .Q(R2), .clk(Clock), .clr(Reset));  // open: en
  Register #(.width(16), .trigger("falling")) u_R3 (
    .D(n16_bit_transistor_4_p3), .Q(R3), .clk(Clock), .clr(Reset));  // open: en
  Register #(.width(16), .trigger("falling")) u_R4 (
    .D(n16_bit_transistor_5_p3), .Q(R4), .clk(Clock), .clr(Reset));  // open: en
  Register #(.width(16), .trigger("falling")) u_R5 (
    .D(n16_bit_transistor_6_p3), .Q(R5), .clk(Clock), .clr(Reset));  // open: en
  Register #(.width(16), .trigger("falling")) u_R6 (
    .D(n16_bit_transistor_7_p3), .Q(R6), .clk(Clock), .clr(Reset));  // open: en
  Register #(.width(16), .trigger("falling")) u_R7 (
    .D(n16_bit_transistor_8_p3), .Q(R7), .clk(Clock), .clr(Reset));  // open: en
endmodule
