// Logisim project Total.circ as structural Verilog: 10 circuits, main circuit main
module main (
  input  Reset,
  input  ResetRAM
);

  wire Clock, Clock_out, CTRL, Exec, Fetch, getcst_1_imm, Load, ramctrl_1_memload, ramctrl_1_memstore, Store,
       WriteReg;
  wire [2:0] GetOp;
  wire [15:0] Addr, alu_1_output, getcst_1_cst, JMP_Address, MemIN, PC, R0, R1, R2, R3, R4, R5, R6, R7,
       registres_1_out_sr1, registres_1_out_sr2;
  wire [31:0] bit_extender_1_out, IR, MemOUT;

  Clock u_Clock (.out(Clock_out));
  Seq seq_1 (.ClockOrig(Clock_out), .reset(Reset), .Fetch(Fetch), .Exec(Exec), .Clock(Clock));
  LED led_1 (.in(Clock_out));
  RegPC regpc_1 (.JMP_Address(JMP_Address), .Cond(1'b0), .CTRL(CTRL), .Clock(Exec), .Reset(Reset), .PC(PC));
  // Probe on PC
  GetAddr getaddr_1 (.PC(PC), .Addr(Addr), .Fetch(Fetch), .Load(Load), .Store(Store));
  // Probe on Addr
  LED led_2 (.in(Fetch));
  LED led_3 (.in(Exec));
  // Probe on MemIN
  assign bit_extender_1_out = {{16{MemIN[15]}}, MemIN};  // Bit_Extender bit_extender_1
  // Probe on PC
  // Probe on IR
  DecodeIR decodeir_1 (
    .CTRL(CTRL), .WriteReg(WriteReg), .IR(IR), .Load(Load), .GetOp(GetOp), .JMPAddress(JMP_Address),
    .Store(Store));
  RamCtrl ramctrl_1 (
    .Store(Store), .Fetch(Fetch), .Exec(Exec), .Load(Load), .MemStore(ramctrl_1_memstore),
    .MemLoad(ramctrl_1_memload), .Clock(Clock));
  // Probe on MemOUT
  RAM #(.addrWidth(16), .dataWidth(32), .bus("separate")) ram_1 (
    .addr(Addr), .din(bit_extender_1_out), .data(MemOUT), .str(ramctrl_1_memstore), .clk(ramctrl_1_memstore),
    .ld(ramctrl_1_memload), .clr(ResetRAM));  // open: sel
  // Probe on R0
  // Probe on R3
  // Probe on R6
  Register #(.width(32), .trigger("falling")) RegIR (.D(MemOUT), .Q(IR), .clk(Fetch), .clr(Reset));  // open: en
  // Probe on R1
  // Probe on R4
  // Probe on R7
  // Probe on IR
  // Probe on R2
  // Probe on R5
  // Probe on IR[8:6]
  // Probe on IR[11:9]
  // Probe on IR[14:12]
  // Probe on getcst_1_cst
  GetCst getcst_1 (.IR(IR), .Cst(getcst_1_cst), .Imm(getcst_1_imm));
  Registres registres_1 (
    .SR1(IR[11:9]), .IN(alu_1_output), .SR2(IR[14:12]), .WriteReg(WriteReg), .DR(IR[8:6]),
    .OUT_SR1(registres_1_out_sr1), .OUT_SR2(registres_1_out_sr2), .OUT_DR(MemIN), .R0(R0), .R1(R1), .R2(R2),
    .R3(R3), .R4(R4), .R5(R5), .R6(R6), .R7(R7), .Reset(Reset), .Clock(Exec));
  // Probe on registres_1_out_sr1
  // Probe on registres_1_out_sr2
  ALU alu_1 (
    .Imm(getcst_1_imm), .e2(GetOp), .Input1(registres_1_out_sr1), .Input2(registres_1_out_sr2),
    .Cst(getcst_1_cst), .Output(alu_1_output));
  // Probe on alu_1_output
  // Probe on R0
  // Probe on R1
  // Probe on R2
  // Probe on R3
  // Probe on R4
  // Probe on R5
  // Probe on R6
  // Probe on R7
  // Probe on alu_1_output

  // Notes on the sheet:
  //   RAM
endmodule

module ALU (
  input  [15:0] Input1,
  input  [15:0] Input2,
  input  [15:0] Cst,
  input  Imm,
  input  [2:0] e2,
  output [15:0] Output
);
endmodule

module DecodeIR (
  input  [31:0] IR,
  output WriteReg,
  output Store,
  output Load,
  output CTRL,
  output [2:0] GetOp,
  output [15:0] JMPAddress
);


  assign CTRL = 1'b0;
  assign GetOp = 3'b000;
  assign JMPAddress = {16{1'b0}};
  assign Load = 1'b0;
  assign Store = 1'b0;
  assign WriteReg = 1'b1;
endmodule

module GetAddr (
  input  [15:0] PC,
  input  Load,
  input  Store,
  input  Fetch,
  output [15:0] Addr
);
endmodule

module GetCst (
  input  [31:0] IR,
  output [15:0] Cst,
  output Imm
);

  Bit_Extender #(.in_width(20)) bit_extender_1 (.in(IR[31:12]), .out(Cst));

  assign Imm = IR[5];
endmodule

module RamCtrl (
  input  Clock,
  input  Exec,
  input  Fetch,
  input  Load,
  input  Store,
  output MemLoad,
  output MemStore
);

  wire and_1_out;

  and and_1 (and_1_out, Exec, Load);
  and and_2 (MemStore, Exec, Clock, Store);
  or or_1 (MemLoad, Fetch, and_1_out);
endmodule

module Registres (
  input  [15:0] IN,
  input  [2:0] SR1,
  input  [2:0] SR2,
  input  [2:0] DR,
  input  WriteReg,
  input  Clock,
  input  Reset,
  output [15:0] R0,
  output [15:0] OUT_SR1,
  output [15:0] R1,
  output [15:0] R2,
  output [15:0] R3,
  output [15:0] OUT_SR2,
  output [15:0] R4,
  output [15:0] R5,
  output [15:0] OUT_DR,
  output [15:0] R6,
  output [15:0] R7
);

  wire demultiplexer_1_out0, demultiplexer_1_out1, demultiplexer_1_out2, demultiplexer_1_out3,
       demultiplexer_1_out4, demultiplexer_1_out5, demultiplexer_1_out6, demultiplexer_1_out7;
  wire [15:0] n16_bit_transistor_1_arith, n16_bit_transistor_2_arith, n16_bit_transistor_3_arith,
       n16_bit_transistor_4_arith, n16_bit_transistor_5_arith, n16_bit_transistor_6_arith,
       n16_bit_transistor_7_arith, n16_bit_transistor_8_arith;

  Demultiplexer #(.select(3)) demultiplexer_1 (
    .out0(demultiplexer_1_out0), .out1(demultiplexer_1_out1), .out2(demultiplexer_1_out2),
    .out3(demultiplexer_1_out3), .out4(demultiplexer_1_out4), .out5(demultiplexer_1_out5),
    .out6(demultiplexer_1_out6), .out7(demultiplexer_1_out7), .in(Clock), .sel(DR), .en(WriteReg));
  _16_bit_transistor u_16_bit_transistor_1 (.Test(demultiplexer_1_out0), .in_1(IN), .Arith(n16_bit_transistor_1_arith));
  _16_bit_transistor u_16_bit_transistor_2 (.Test(demultiplexer_1_out1), .in_1(IN), .Arith(n16_bit_transistor_2_arith));
  _16_bit_transistor u_16_bit_transistor_3 (.Test(demultiplexer_1_out2), .in_1(IN), .Arith(n16_bit_transistor_3_arith));
  _16_bit_transistor u_16_bit_transistor_4 (.Test(demultiplexer_1_out3), .in_1(IN), .Arith(n16_bit_transistor_4_arith));
  _16_bit_transistor u_16_bit_transistor_5 (.Test(demultiplexer_1_out4), .in_1(IN), .Arith(n16_bit_transistor_5_arith));
  _16_bit_transistor u_16_bit_transistor_6 (.Test(demultiplexer_1_out5), .in_1(IN), .Arith(n16_bit_transistor_6_arith));
  _16_bit_transistor u_16_bit_transistor_7 (.Test(demultiplexer_1_out6), .in_1(IN), .Arith(n16_bit_transistor_7_arith));
  _16_bit_transistor u_16_bit_transistor_8 (.Test(demultiplexer_1_out7), .in_1(IN), .Arith(n16_bit_transistor_8_arith));
  Register #(.width(16), .trigger("falling")) u_R0 (
    .D(n16_bit_transistor_1_arith), .Q(R0), .clk(Clock), .clr(Reset));  // open: en
  Register #(.width(16), .trigger("falling")) u_R1 (
    .D(n16_bit_transistor_2_arith), .Q(R1), .clk(Clock), .clr(Reset));  // open: en
  Register #(.width(16), .trigger("falling")) u_R2 (
    .D(n16_bit_transistor_3_arith), .Q(R2), .clk(Clock), .clr(Reset));  // open: en
  Register #(.width(16), .trigger("falling")) u_R3 (
    .D(n16_bit_transistor_4_arith), .Q(R3), .clk(Clock), .clr(Reset));  // open: en
  Register #(.width(16), .trigger("falling")) u_R4 (
    .D(n16_bit_transistor_5_arith), .Q(R4), .clk(Clock), .clr(Reset));  // open: en
  Register #(.width(16), .trigger("falling")) u_R5 (
    .D(n16_bit_transistor_6_arith), .Q(R5), .clk(Clock), .clr(Reset));  // open: en
  Register #(.width(16), .trigger("falling")) u_R6 (
    .D(n16_bit_transistor_7_arith), .Q(R6), .clk(Clock), .clr(Reset));  // open: en
  Register #(.width(16), .trigger("falling")) u_R7 (
    .D(n16_bit_transistor_8_arith), .Q(R7), .clk(Clock), .clr(Reset));  // open: en
  Multiplexer #(.select(3), .width(16)) multiplexer_1 (
    .in0(R0), .in1(R1), .in2(R2), .in3(R3), .in4(R4), .in5(R5), .in6(R6), .in7(R7), .out(OUT_SR1), .sel(SR1));  // open: en
  Multiplexer #(.select(3), .width(16)) multiplexer_2 (
    .out(OUT_SR2), .sel(SR2));  // open: in0, in1, in2, in3, in4, in5, in6, in7, en
  Multiplexer #(.select(3), .width(16)) multiplexer_3 (
    .out(OUT_DR), .sel(DR));  // open: in0, in1, in2, in3, in4, in5, in6, in7, en
endmodule

module RegPC (
  input  [15:0] JMP_Address,
  input  Cond,
  input  CTRL,
  input  Clock,
  input  Reset,
  output [15:0] PC
);

  Register #(.width(16), .trigger("falling")) u_PC (.Q(PC), .clk(Clock), .clr(Reset));  // open: D, en
endmodule

module Seq (
  input  ClockOrig,
  input  reset,
  output Fetch,
  output Exec,
  output Clock
);

  Register #(.width(1), .trigger("falling")) register_1 (
    .D(Fetch), .Q(Exec), .clk(ClockOrig), .clr(reset));  // open: en
  not not_1 (Fetch, Exec);
  buf buffer_1 (Clock, ClockOrig);
endmodule

module _16_bit_transistor (
  input  [15:0] in_1,
  input  Test,
  output [15:0] Arith
);

  and and_1 (Arith[0], in_1[0], Test);
  and and_2 (Arith[1], in_1[1], Test);
  and and_3 (Arith[2], in_1[2], Test);
  and and_4 (Arith[3], in_1[3], Test);
  and and_5 (Arith[4], in_1[4], Test);
  and and_6 (Arith[5], in_1[5], Test);
  and and_7 (Arith[6], in_1[6], Test);
  and and_8 (Arith[7], in_1[7], Test);
  and and_9 (Arith[8], in_1[8], Test);
  and and_10 (Arith[9], in_1[9], Test);
  and and_11 (Arith[10], in_1[10], Test);
  and and_12 (Arith[11], in_1[11], Test);
  and and_13 (Arith[12], in_1[12], Test);
  and and_14 (Arith[13], in_1[13], Test);
  and and_15 (Arith[14], in_1[14], Test);
  and and_16 (Arith[15], in_1[15], Test);
endmodule
